# Fritzing sketch graph (saved by Fritzing 0.9.4)
breadboards: 2

parts:
  arduino = Arduino Uno (Rev3)
  PIR1 = PIR sensor
  LED1 = LED - 5mm [color="Red (633nm)" package="5 mm [THT]"]
  LED2 = LED - 5mm [color="Red (633nm)" package="5 mm [THT]"]
  R1 = Resistor [tolerance=±5% resistance=220 package=THT]
  R2 = Resistor [tolerance=±5% resistance=220 package=THT]

nets:
  N1: arduino.D8, R1.Pin_0
  N2: arduino.D10_PWM/SS, R2.Pin_0
  GND: arduino.GND, PIR1.GND, LED1.cathode, LED2.cathode
  N3: arduino.D2, PIR1.SIG
  3V3: arduino.3V3, PIR1.VDD
  N4: LED1.anode, R1.Pin_1
  N5: LED2.anode, R2.Pin_1
